// Logisim project SevenSegDec.circ as structural Verilog: 1 circuit, main circuit SevenSegDec
module SevenSegDec (
  input  A3,
  input  A2,
  input  A1,
  input  A0,
  output S0,
  output S1,
  output S2,
  output S3,
  output S4,
  output S5,
  output S6
);

  wire not_1_out, not_2_out, not_3_out, not_4_out, not_5_out, not_6_out, not_7_out, not_8_out, not_9_out,
       not_10_out, not_11_out, not_12_out, not_13_out, not_14_out, not_15_out, not_16_out, or_1_out,
       or_2_out, or_3_out, or_4_out, or_5_out, or_6_out, or_7_out, or_8_out, or_12_out, or_13_out, or_14_out,
       or_15_out;

  not not_1 (not_1_out, A2);
  not not_2 (not_2_out, A3);
  not not_3 (not_3_out, A2);
  not not_4 (not_4_out, A1);
  not not_5 (not_5_out, A0);
  not not_6 (not_6_out, A1);
  not not_7 (not_7_out, A2);
  not not_8 (not_8_out, A1);
  or or_1 (or_1_out, A3, not_7_out, not_8_out, A0);
  or or_2 (or_2_out, A3, not_2_out);
  or or_3 (or_3_out, A2, not_3_out);
  or or_4 (or_4_out, A1, not_4_out);
  or or_5 (or_5_out, A0, not_5_out);
  or or_6 (or_6_out, not_1_out, A3, A1, A0);
  or or_7 (or_7_out, not_6_out, A0, A2, A3);
  not not_9 (not_9_out, A3);
  or or_8 (or_8_out, not_9_out, A2, A1, A0);
  and and_1 (S4, or_8_out, or_1_out, or_6_out);
  not not_10 (not_10_out, A2);
  not not_11 (not_11_out, A0);
  or or_9 (S2, or_2_out, or_3_out, or_4_out, or_5_out);
  or or_10 (S3, not_11_out, A3, A1, A2);
  not not_12 (not_12_out, A0);
  not not_13 (not_13_out, A1);
  or or_11 (S6, A3, A2, A1, A0);
  or or_12 (or_12_out, not_12_out, not_13_out, not_10_out, A3);
  _7_Segment_Display u_7_segment_display_1 (.g(S0), .f(S1), .a(S2), .b(S3), .e(S4), .d(S2), .c(S6));  // open: dp
  not not_14 (not_14_out, A1);
  not not_15 (not_15_out, A2);
  or or_13 (or_13_out, A0, not_14_out, not_15_out, A3);
  and and_2 (S0, or_7_out, or_12_out);
  not not_16 (not_16_out, A3);
  or or_14 (or_14_out, A1, not_16_out, A2, A0);
  and and_3 (S1, or_13_out, or_14_out, or_15_out);
  or or_15 (or_15_out, A0, A3, A1, A2);

  assign S5 = S2;

  // Notes on the sheet:
  //   YIMEI YANG, 260898303
endmodule
