// Logisim project SequentialDivider.circ as structural Verilog: 1 circuit, main circuit Divider
module Divider (
  input  [3:0] Dividend,
  input  in_2,
  input  in_3,
  input  [3:0] Divisor,
  input  in_5,
  input  RESET,
  output [3:0] Quotient,
  output [3:0] Remainder,
  output DONE
);

  wire clock_1_out, not_1_out, not_2_out, or_1_out, subtractor_1_bout;
  wire [2:0] counter_1_q;
  wire [7:0] multiplexer_1_out, shift_register_1_out, subtractor_1_out;
  wire [7:4] register_1_q;

  Clock clock_1 (.out(clock_1_out));
  Shift_Register shift_register_1 (
    .in(in_5), .clk(clock_1_out), .out(shift_register_1_out[0]), .load(RESET), .d0(Divisor[3]),
    .q0(shift_register_1_out[7]), .d1(Divisor[2]), .q1(shift_register_1_out[6]), .d2(Divisor[1]),
    .q2(shift_register_1_out[5]), .d3(Divisor[0]), .q3(shift_register_1_out[4]), .d4(in_3),
    .q4(shift_register_1_out[3]), .d5(in_3), .q5(shift_register_1_out[2]), .d6(in_3),
    .q6(shift_register_1_out[1]), .d7(in_3));  // open: shift, clr, q7
  Counter #(.max('h7), .width(3)) counter_1 (
    .Q(counter_1_q), .clk(clock_1_out), .clr(RESET));  // open: load, D, count, carry, up
  Subtractor subtractor_1 (
    .a({register_1_q, Remainder}), .b(shift_register_1_out), .out(subtractor_1_out), .bout(subtractor_1_bout));  // open: bin
  not not_1 (not_1_out, counter_1_q[1]);
  and and_1 (DONE, counter_1_q[0], not_1_out, counter_1_q[2]);
  Multiplexer #(.enable("false"), .width(8)) multiplexer_1 (
    .in0(subtractor_1_out), .in1({{4{in_2}}, Dividend}), .out(multiplexer_1_out), .sel(RESET));
  not not_2 (not_2_out, subtractor_1_bout);
  or or_1 (or_1_out, not_2_out, RESET);
  Shift_Register #(.length(4)) shift_register_2 (
    .in(not_2_out), .clk(clock_1_out), .out(Quotient[3]), .clr(RESET), .q0(Quotient[0]), .q1(Quotient[1]),
    .q2(Quotient[2]));  // open: shift, load, d0, d1, d2, d3, q3
  Register register_1 (
    .D(multiplexer_1_out), .en(or_1_out), .Q({register_1_q, Remainder}), .clk(clock_1_out));  // open: clr

  // Notes on the sheet:
  //   Yimei YANG, 260898303
endmodule
