// Logisim project SequentialMultipler.circ as structural Verilog: 1 circuit, main circuit Multiplier
module Multiplier (
  input  in_1,
  input  [3:0] A,
  input  in_3,
  input  [3:0] B,
  input  in_5,
  input  RESET,
  output [7:0] PRODUCT,
  output DONE
);

  wire clock_1_out, not_1_out, shift_register_2_out;
  wire [2:0] counter_1_q;
  wire [7:0] adder_1_out, shift_register_1_q0;

  Clock clock_1 (.out(clock_1_out));
  Shift_Register shift_register_1 (
    .in(in_3), .clk(clock_1_out), .out(shift_register_1_q0[7]), .load(RESET), .d0(A[0]),
    .q0(shift_register_1_q0[0]), .d1(A[1]), .q1(shift_register_1_q0[1]), .d2(A[2]),
    .q2(shift_register_1_q0[2]), .d3(A[3]), .q3(shift_register_1_q0[3]), .d4(in_1),
    .q4(shift_register_1_q0[4]), .d5(in_1), .q5(shift_register_1_q0[5]), .d6(in_1),
    .q6(shift_register_1_q0[6]), .d7(in_1));  // open: shift, clr, q7
  Shift_Register #(.length(4)) shift_register_2 (
    .in(in_5), .clk(clock_1_out), .out(shift_register_2_out), .load(RESET), .d0(B[3]), .d1(B[2]), .d2(B[1]),
    .d3(B[0]));  // open: shift, clr, q0, q1, q2, q3
  Counter #(.max('h7), .width(3)) counter_1 (
    .Q(counter_1_q), .clk(clock_1_out), .clr(RESET));  // open: load, D, count, carry, up
  not not_1 (not_1_out, counter_1_q[1]);
  and and_1 (DONE, counter_1_q[0], not_1_out, counter_1_q[2]);
  Adder adder_1 (.a(shift_register_1_q0), .b(PRODUCT), .out(adder_1_out));  // open: cin, cout
  Register register_1 (.D(adder_1_out), .en(shift_register_2_out), .Q(PRODUCT), .clk(clock_1_out), .clr(RESET));

  // Notes on the sheet:
  //   Yimei YANG, 260898303
endmodule
