// Logisim project led.circ as structural Verilog: 1 circuit, main circuit main
module main (
);

  wire and_1_out, and_2_out, and_3_out, and_4_out, and_5_out, and_6_out, and_7_out, and_8_out, and_9_out,
       clock_1_out, d_ff_1_q, d_ff_1_qn, d_ff_2_q, d_ff_2_qn, d_ff_3_q, d_ff_3_qn, d_ff_4_q, d_ff_4_qn,
       not_1_out, not_2_out, not_3_out, not_4_out, not_5_out, not_6_out, not_7_out, not_8_out, undriven,
       undriven_2, undriven_3, undriven_4, xor_1_out, xor_2_out, xor_3_out;

  and and_1 (and_1_out, d_ff_1_q, not_5_out, not_6_out, not_8_out);
  and and_2 (and_2_out, not_3_out, not_6_out, not_2_out, d_ff_2_q);
  not not_1 (not_1_out, d_ff_1_q);
  not not_2 (not_2_out, d_ff_1_q);
  D_Flip_Flop d_ff_1 (.clk(d_ff_2_qn), .D(d_ff_1_qn), .Q(d_ff_1_q), .Qn(d_ff_1_qn));  // open: preset, reset
  not not_3 (not_3_out, d_ff_4_q);
  and and_3 (and_3_out, not_2_out, not_4_out, not_6_out, d_ff_4_q);
  not not_4 (not_4_out, d_ff_2_q);
  D_Flip_Flop d_ff_2 (.clk(d_ff_3_qn), .D(d_ff_2_qn), .Q(d_ff_2_q), .Qn(d_ff_2_qn));  // open: preset, reset
  and and_4 (and_4_out, d_ff_2_q, not_2_out, d_ff_4_q, not_6_out);
  D_Flip_Flop d_ff_3 (.clk(d_ff_4_qn), .D(d_ff_3_qn), .Q(d_ff_3_q), .Qn(d_ff_3_qn));  // open: preset, reset
  not not_5 (not_5_out, d_ff_2_q);
  xor xor_1 (xor_1_out, and_2_out, and_7_out);
  not not_6 (not_6_out, d_ff_3_q);
  and and_5 (and_5_out, not_1_out, not_5_out, d_ff_3_q, not_8_out);
  D_Flip_Flop d_ff_4 (.clk(clock_1_out), .D(d_ff_4_qn), .Q(d_ff_4_q), .Qn(d_ff_4_qn));  // open: preset, reset
  not not_7 (not_7_out, d_ff_4_q);
  Clock clock_1 (.out(clock_1_out));
  not not_8 (not_8_out, d_ff_4_q);
  and and_6 (and_6_out, not_1_out, not_5_out, d_ff_3_q, d_ff_4_q);
  and and_7 (and_7_out, not_2_out, d_ff_2_q, d_ff_3_q, not_7_out);
  and and_8 (and_8_out, not_6_out, not_4_out, d_ff_1_q, d_ff_4_q);
  LED led_1 (.in(xor_2_out));
  and and_9 (and_9_out, not_2_out, d_ff_4_q, d_ff_3_q, d_ff_2_q);
  xor xor_2 (xor_2_out, and_6_out, and_1_out);
  LED led_2 (.in(undriven));
  LED led_3 (.in(and_3_out));
  LED led_4 (.in(undriven_2));
  LED led_5 (.in(xor_3_out));
  xor xor_3 (xor_3_out, and_9_out, and_8_out);
  LED led_6 (.in(undriven_3));
  LED led_7 (.in(and_5_out));
  LED led_8 (.in(undriven_4));
  LED led_9 (.in(xor_1_out));
  LED led_10 (.in(and_4_out));

  // Notes on the sheet:
  //   1
  //   0
  //   2
  //   3
  //   Yimei YANG, 260898303
  //   5
  //   4
  //   6
  //   7
  //   8
  //   9
endmodule
